// Logisim project Versuch1.circ as structural Verilog: 7 circuits, main circuit main
module main (
  input  in_1,
  input  in_2,
  output out_3
);

  NAND_NMOS nand_nmos_1 (.X0(in_1), .X1(in_2), .Y(out_3));
endmodule

module NAND_NMOS (
  input  X0,
  input  X1,
  output Y
);

  wire transistor_2_out;

  Pull_Resistor #(.pull(1)) pull_resistor_1 (.node(Y));
  Transistor #(.\type ("n")) transistor_1 (.in(transistor_2_out), .out(Y), .gate(X0));
  Transistor #(.\type ("n")) transistor_2 (.in(1'b0), .out(transistor_2_out), .gate(X1));

  // Notes on the sheet:
  //   Marcel Syben
  //   Eduard Wilms
  //   Benedikt Ottens
  //   27.10.20
endmodule

module NAND_CMOS (
  input  X0,
  input  X1,
  output out_3
);

  wire transistor_4_out;

  Transistor transistor_1 (.in(1'b1), .out(out_3), .gate(X0));
  Transistor transistor_2 (.in(1'b1), .out(out_3), .gate(X1));
  Transistor #(.\type ("n")) transistor_3 (.in(transistor_4_out), .out(out_3), .gate(X0));
  Transistor #(.\type ("n")) transistor_4 (.in(1'b0), .out(transistor_4_out), .gate(X1));

  // Notes on the sheet:
  //   27.10.20
  //   Marcel Syben
  //   Eduard Wilms
  //   Benedikt Ottens
endmodule

module main2 (
  input  X0,
  input  X1,
  input  in_3,
  output out_4,
  output out_5
);

  CMOS_INV cmos_inv_1 (._27_10_20(in_3), .out_2(out_5));
  NAND_CMOS nand_cmos_1 (.X0(X0), .X1(X1), .out_3(out_4));
endmodule

module NOR_CMOS (
  input  in_1,
  input  in_2,
  output out_3
);

  wire transistor_2_out;

  Transistor #(.\type ("n")) transistor_1 (.in(1'b0), .out(out_3), .gate(in_2));
  Transistor transistor_2 (.in(1'b1), .out(transistor_2_out), .gate(in_1));
  Transistor transistor_3 (.in(transistor_2_out), .out(out_3), .gate(in_2));
  Transistor #(.\type ("n")) transistor_4 (.in(1'b0), .out(out_3), .gate(in_1));

  // Notes on the sheet:
  //   Marcel Syben
  //   Eduard Wilms
  //   Benedikt Ottens
  //   27.10.20
endmodule

module CMOS_INV (
  input  _27_10_20,
  output out_2
);

  Transistor transistor_1 (.in(1'b1), .out(out_2), .gate(_27_10_20));
  Transistor #(.\type ("n")) transistor_2 (.in(1'b0), .out(out_2), .gate(_27_10_20));

  // Notes on the sheet:
  //   Marcel Syben
  //   Eduard Wilms
  //   Benedikt Ottens
endmodule

module CMOS_XOR (
  input  in_1,
  input  in_2,
  output out_3
);

  wire cmos_inv_1_out_2, cmos_inv_2_out_2, nand_cmos_1_out_3, nand_cmos_2_out_3;

  CMOS_INV cmos_inv_1 (._27_10_20(in_2), .out_2(cmos_inv_1_out_2));
  CMOS_INV cmos_inv_2 (._27_10_20(in_1), .out_2(cmos_inv_2_out_2));
  NAND_CMOS nand_cmos_1 (.X0(in_1), .X1(cmos_inv_1_out_2), .out_3(nand_cmos_1_out_3));
  NAND_CMOS nand_cmos_2 (.X0(in_2), .X1(cmos_inv_2_out_2), .out_3(nand_cmos_2_out_3));
  NAND_CMOS nand_cmos_3 (.X0(nand_cmos_1_out_3), .X1(nand_cmos_2_out_3), .out_3(out_3));

  // Notes on the sheet:
  //   Marcel Syben
  //   27.10.20
  //   Eduard Wilms
  //   Benedikt Ottens
endmodule
