// Logisim project Versuch2.circ as structural Verilog: 2 circuits, main circuit main
module main (
  input  X0,
  input  X1,
  input  X2,
  input  X3,
  output out_5
);

  wire nand_1_out, nand_2_out, nand_3_out, not_1_out, not_2_out;

  not not_1 (not_1_out, X0);
  not not_2 (not_2_out, X1);
  nand nand_1 (nand_1_out, not_1_out, not_2_out);
  nand nand_2 (nand_2_out, X1, X3);
  nand nand_3 (nand_3_out, X2, X3);
  nand nand_4 (out_5, nand_1_out, nand_2_out, nand_3_out);

  // Notes on the sheet:
  //   Marcel Syben
  //   Eduard Wilms
  //   Benedikt Otten
  //   17.11.20
  //   Disjunktiv
endmodule

module konj (
  input  X0,
  input  X1,
  input  X2,
  input  X3,
  output Y
);

  wire nand_1_out, nand_2_out, nand_3_out, nand_4_out, not_1_out, not_2_out, not_3_out;

  not not_1 (not_1_out, X3);
  not not_2 (not_2_out, X3);
  not not_3 (not_3_out, X2);
  nand nand_1 (nand_1_out, X0, not_1_out);
  nand nand_2 (nand_2_out, X1, not_2_out);
  nand nand_3 (nand_3_out, X0, not_3_out);
  nand nand_4 (nand_4_out, nand_1_out, nand_2_out, nand_3_out);
  not not_4 (Y, nand_4_out);

  // Notes on the sheet:
  //   17.11.20
  //   Marcel Syben
  //   Eduard Wilms
  //   Benedikt Otten
  //   Konjunktiv
endmodule
