// Logisim project Versuch3.circ as structural Verilog: 4 circuits, main circuit main
module main (
  input  in_1,
  input  in_2,
  input  in_3,
  output out_4
);

  wire nand_1_out, nand_2_out, nand_3_out;

  nand nand_1 (nand_1_out, in_1, in_2);
  nand nand_2 (nand_2_out, in_1, in_3);
  nand nand_3 (nand_3_out, in_2, in_3);
  nand nand_4 (out_4, nand_1_out, nand_2_out, nand_3_out);
endmodule

module VA1 (
  input  A,
  input  B,
  input  C,
  output S0
);

  wire nand_1_out, xor_1_out;

  ExactlyOne xor_1 (.out(xor_1_out), .in0(A), .in1(B), .in2(C));
  nand nand_1 (nand_1_out, A, B, C);
  xor xor_2 (S0, xor_1_out, ~nand_1_out);  // XOR_Gate
  // NAND_Gate nand_2 is placed but not wired
endmodule

module VA2 (
  input  in_1,
  input  in_2,
  input  in_3,
  output out_4
);

  wire n7410_1_pin8, n7486_1_pin4, n7486_1_pin5, n7486_1_pin11;

  _7486 #(.ShowInternalStructure("true")) u_7486_1 (
    .pin4(n7486_1_pin4), .pin5(n7486_1_pin5), .pin6(out_4), .pin13(in_1), .pin12(in_2),
    .pin11(n7486_1_pin11), .pin10(n7486_1_pin11), .pin9(in_3), .pin8(n7486_1_pin5));  // open: pin1, pin2, pin3
  _7410 #(.ShowInternalStructure("true")) u_7410_1 (
    .pin11(in_3), .pin10(in_2), .pin9(in_1), .pin8(n7410_1_pin8));  // open: pin1, pin2, pin3, pin4, pin5, pin6, pin13, pin12
  _7400 #(.ShowInternalStructure("true")) u_7400_1 (
    .pin13(n7410_1_pin8), .pin12(n7410_1_pin8), .pin11(n7486_1_pin4));  // open: pin1, pin2, pin3, pin4, pin5, pin6, pin10, pin9, pin8
endmodule

module Anzeige (
  input  [3:0] in_1
);

  wire [6:0] encoder_data;

  ROM #(.addrWidth(4), .dataWidth(7)) encoder (.addr(in_1), .data(encoder_data));
  _7_Segment_Display sseg (
    .g(encoder_data[6]), .f(encoder_data[5]), .a(encoder_data[0]), .b(encoder_data[1]), .e(encoder_data[4]),
    .d(encoder_data[3]), .c(encoder_data[2]));  // open: dp

  // Notes on the sheet:
  //   contents of encoder (hex, n*v repeats v):
  //   3f 6 5b 4f 26 6d 7d 7 7f 6f 77 7c 39 5e 79 71
endmodule
