// Logisim project 5.circ as structural Verilog: 2 circuits, main circuit Zaehler
module Zaehler (
  input  CLK,
  output TC
);

  wire and_1_out, and_2_out, and_3_out, t_ff_1_q, t_ff_2_q, t_ff_3_q, t_ff_4_q;

  T_Flip_Flop t_ff_1 (.T(1'b1), .clk(CLK), .Q(t_ff_1_q));  // open: Qn, reset, preset
  T_Flip_Flop t_ff_2 (.T(and_1_out), .clk(CLK), .Q(t_ff_2_q));  // open: Qn, reset, preset
  T_Flip_Flop t_ff_3 (.T(and_2_out), .clk(CLK), .Q(t_ff_3_q));  // open: Qn, reset, preset
  T_Flip_Flop t_ff_4 (.T(and_3_out), .clk(CLK), .Q(t_ff_4_q));  // open: Qn, reset, preset
  and and_1 (and_1_out, 1'b1, t_ff_1_q);
  and and_2 (and_2_out, and_1_out, t_ff_2_q);
  and and_3 (and_3_out, and_2_out, t_ff_3_q);
  and and_4 (TC, and_3_out, t_ff_4_q);

  // Notes on the sheet:
  //   Marcel Syben
  //   Benedikt Otten
  //   Eduard Wilms
  //   05.01.21
endmodule

module Ampel (
);

  wire and_1_out, and_2_out, and_3_out, and_4_out, and_5_out, and_6_out, CLK_out, CTR_tc, not_1_out,
       or_1_out, or_2_out, Z0_q, Z1_q;

  Clock CLK (.out(CLK_out));
  D_Flip_Flop Z1 (.D(or_1_out), .clk(CLK_out), .Q(Z1_q));  // open: Qn, preset, reset
  D_Flip_Flop Z0 (.D(or_2_out), .clk(CLK_out), .Q(Z0_q));  // open: Qn, preset, reset
  Zaehler CTR (.CLK(CLK_out), .TC(CTR_tc));
  and and_1 (and_1_out, ~CTR_tc, Z1_q);  // AND_Gate
  and and_2 (and_2_out, Z1_q, ~Z0_q);  // AND_Gate
  and and_3 (and_3_out, Z0_q, CTR_tc, ~Z1_q);  // AND_Gate
  and and_4 (and_4_out, Z0_q, ~CTR_tc);  // AND_Gate
  and and_5 (and_5_out, CTR_tc, ~Z0_q);  // AND_Gate
  or or_1 (or_1_out, and_1_out, and_2_out, and_3_out);
  or or_2 (or_2_out, and_4_out, and_5_out);
  not not_1 (not_1_out, Z1_q);
  and and_6 (and_6_out, Z1_q, ~Z0_q);  // AND_Gate
  LED ROT (.in(not_1_out));
  LED GELB (.in(Z0_q));
  LED GRUEN (.in(and_6_out));

  // Notes on the sheet:
  //   Marcel Syben
  //   Benedikt Otten
  //   Eduard Wilms
  //   05.01.21
endmodule
